# Fritzing sketch RobotElectronics Sketch (saved by Fritzing 0.9.3b)
breadboards: 1

parts:
  BLMC2 = DIP - 40 pins [chip_label=ODrive package="DIP (Dual Inline) [THT]"]
  Part1 = Adafruit LSM6DS33 6-DoF Accel + Gyro IMU [part_number="Adafruit #4480"]
  BLMC6 = DIP - 40 pins [chip_label=ODrive package="DIP (Dual Inline) [THT]"]
  IC5 = DIP - 40 pins [chip_label=ODrive package="DIP (Dual Inline) [THT]"]
  BLMC3 = DIP - 40 pins [chip_label=ODrive package="DIP (Dual Inline) [THT]"]
  BLMC4 = DIP - 40 pins [chip_label=ODrive package="DIP (Dual Inline) [THT]"]
  BLMC7 = DIP - 40 pins [chip_label=ODrive package="DIP (Dual Inline) [THT]"]
  BLMC5 = DIP - 40 pins [chip_label=ODrive package="DIP (Dual Inline) [THT]"]
  A3 = Drok DC buck module
  A1 = Orange PI 5
  18V2 = Battery Holders [package=battcon_20mm]
  18V1 = Battery Holders [package=battcon_20mm]
  Motor_1 = DC Motor with tachometer
  Motor_2 = DC Motor with tachometer
  Motor_3 = DC Motor with tachometer
  Motor_4 = DC Motor with tachometer
  Motor_5 = DC Motor with tachometer
  Motor_6 = DC Motor with tachometer
  Motor_7 = DC Motor with tachometer
  Motor_8 = DC Motor with tachometer
  S1 = Pushbutton [package=THT]
  BLMC1 = DIP - 40 pins [chip_label=ODrive package="DIP (Dual Inline) [THT]"]

nets:
  N1: BLMC2.J3_CAN_H, Part1.SCL, BLMC6.J3_CAN_H, IC5.J3_CAN_H, BLMC3.J3_CAN_H, BLMC4.J3_CAN_H, BLMC7.J3_CAN_H, BLMC5.J3_CAN_H, A1.Pin_7, A1.Pin_11, BLMC1.J3_CAN_H
  N2: BLMC2.J3_CAN_L, BLMC6.J3_CAN_L, IC5.J3_CAN_L, BLMC3.J3_CAN_L, BLMC4.J3_CAN_L, BLMC7.J3_CAN_L, BLMC5.J3_CAN_L, A1.Pin_6, BLMC1.J3_CAN_L
  N3: BLMC2.AUX_(-), BLMC6.AUX_(-), IC5.AUX_(-), BLMC3.AUX_(-), BLMC4.AUX_(-), BLMC7.AUX_(-), BLMC5.AUX_(-), 18V2.-, 18V1.-, BLMC1.AUX_(-)
  N4: BLMC2.AUX_(+), BLMC1.AUX_(+)
  N5: BLMC2.M0_MOTOR_PHASE_C, Motor_2.pin2
  N6: BLMC2.M0_MOTOR_PHASE_B, Motor_2.pin3
  N7: BLMC2.M0_MOTOR_PHASE_A, Motor_2.pin1
  N8: Part1.GND, A1.Pin_13
  N9: Part1.SDA, A1.Pin_10
  N10: Part1.3.3V, A1.Pin_1
  N11: BLMC6.AUX_(+), IC5.AUX_(+), BLMC7.AUX_(+), BLMC5.AUX_(+), A3.Pin_2, S1.leg0
  N12: BLMC6.M0_MOTOR_PHASE_C, Motor_6.pin2
  N13: BLMC6.M0_MOTOR_PHASE_B, Motor_6.pin3
  N14: BLMC6.M0_MOTOR_PHASE_A, Motor_6.pin1
  N15: IC5.M0_MOTOR_PHASE_C, Motor_8.pin2
  N16: IC5.M0_MOTOR_PHASE_B, Motor_8.pin3
  N17: IC5.M0_MOTOR_PHASE_A, Motor_8.pin1
  N18: BLMC3.AUX_(+), BLMC4.AUX_(+)
  N19: BLMC3.M0_MOTOR_PHASE_C, Motor_3.pin2
  N20: BLMC3.M0_MOTOR_PHASE_B, Motor_3.pin3
  N21: BLMC3.M0_MOTOR_PHASE_A, Motor_3.pin1
  N22: BLMC4.M0_MOTOR_PHASE_C, Motor_4.pin2
  N23: BLMC4.M0_MOTOR_PHASE_B, Motor_4.pin3
  N24: BLMC4.M0_MOTOR_PHASE_A, Motor_4.pin1
  N25: BLMC7.M0_MOTOR_PHASE_C, Motor_7.pin2
  N26: BLMC7.M0_MOTOR_PHASE_B, Motor_7.pin3
  N27: BLMC7.M0_MOTOR_PHASE_A, Motor_7.pin1
  N28: BLMC5.M0_MOTOR_PHASE_C, Motor_5.pin2
  N29: BLMC5.M0_MOTOR_PHASE_B, Motor_5.pin3
  N30: BLMC5.M0_MOTOR_PHASE_A, Motor_5.pin1
  N31: A3.Pin_1, A3.Pin_4, A1.pin_30
  N32: A3.Pin_3, A1.pin_31
  N33: 18V2.+, 18V1.+, S1.leg1
  N34: Motor_1.pin1, BLMC1.M0_MOTOR_PHASE_A
  N35: Motor_1.pin2, BLMC1.M0_MOTOR_PHASE_C
  N36: Motor_1.pin3, BLMC1.M0_MOTOR_PHASE_B

notes:
  ODrive model is not S1, does not have two motor support

custom parts:
  DIP - 40 pins: A DIP stand-in part for whatever IC you want. With 40 pins on a 300mil dual inline package (DIP) footprint.
  Adafruit LSM6DS33 6-DoF Accel + Gyro IMU: Add motion and orientation sensing to your Arduino project with this affordable 6 Degree of Freedom (6-DoF) sensor with sensors from ST. The board includes an LSM6DS33, a 6-DoF IMU accelerometer + gyro. The 3-axis accelerometer, can tell you which direction is down towards the Earth (by measuring gravity) or how fast the board is accelerating in 3D space. The 3-axis gyroscope that can measure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
  Orange PI 5: Cobbled together Orange Pi 5 Schematic based on Orange Pi 3 LTS Schematic by Peter Van Epp (https://forum.fritzing.org/t/orangepi-3-lts-part-request/22727)
